// Logisim project neuron.circ as structural Verilog: 7 circuits, main circuit main
module main (
  input  Req,
  input  Ack_out,
  input  [3:0] Data,
  output Req_out,
  output Ack,
  output [3:0] Data_out
);

  wire muller_1_z, not_1_out;
  wire [3:0] adder_1_out, register_1_q, register_2_q;

  Register #(.width(4)) register_1 (.D(adder_1_out), .Q(register_1_q), .clk(Req), .clr(not_1_out));  // open: en
  Register #(.width(4)) register_2 (.D(Data), .Q(register_2_q), .clk(Req), .clr(not_1_out));  // open: en
  muller muller_1 (.A(Req), .B(Ack_out), .Z(muller_1_z));  // open: Reset
  Adder #(.width(4)) adder_1 (.a(register_1_q), .b(register_2_q), .out(adder_1_out));  // open: cin, cout
  // Delay delay_1: pin names not known; wires that end beside it: muller_1_z, Ack
  Comparator #(.width(4), .mode("unsigned")) comparator_1 (.a(adder_1_out), .b(4'b1000), .gt(Req_out));  // open: eq, lt
  not not_1 (not_1_out, Ack_out);
  Multiplexer #(.width(4), .enable("false")) multiplexer_1 (
    .in0(4'b0000), .in1(4'b0010), .out(Data_out), .sel(Req_out));
endmodule

module muller (
  input  A,
  input  B,
  input  Reset,
  output Z
);

  wire and_1_out, and_2_out, multiplexer_1_out, multiplexer_2_out, not_1_out, or_1_out;

  Multiplexer multiplexer_1 (.in0(A), .in1(1'b0), .out(multiplexer_1_out), .sel(Reset));  // open: en
  Multiplexer multiplexer_2 (.in0(B), .in1(1'b1), .out(multiplexer_2_out), .sel(Reset));  // open: en
  not not_1 (not_1_out, multiplexer_2_out);
  and and_1 (and_1_out, multiplexer_1_out, not_1_out);
  or or_1 (or_1_out, multiplexer_1_out, not_1_out);
  or or_2 (Z, and_1_out, and_2_out);
  and and_2 (and_2_out, Z, or_1_out);
endmodule

module Network (
  input  in_1,
  input  [3:0] in_2
);

  wire main_1_p2, main_1_p4, main_1_p5, main_1_p6, main_2_p4, main_2_p5, main_2_p6, main_3_p4, main_3_p6,
       not_1_out;

  // Probe on main_1_p2
  // main main_1: pin names not known; wires that end beside it: in_1, main_1_p2, in_2, main_1_p4, main_1_p5, main_1_p6
  // main main_2: pin names not known; wires that end beside it: main_1_p4, main_1_p5, main_1_p6, main_2_p4, main_2_p5, main_2_p6
  not not_1 (not_1_out, main_3_p4);
  // main main_3: pin names not known; wires that end beside it: main_2_p4, main_2_p5, main_2_p6, main_3_p4, not_1_out, main_3_p6
  // Probe on main_3_p6
endmodule

module Delay (
  input  In,
  input  [3:0] in_2,
  output Out
);

  wire clock_1_out, comparator_1_gt, d_ff_1_q, not_1_out;
  wire [3:0] adder_1_out, register_1_q;

  Clock clock_1 (.out(clock_1_out));
  Adder #(.width(4)) adder_1 (.a(register_1_q), .b(4'b0001), .out(adder_1_out));  // open: cin, cout
  Register #(.width(4)) register_1 (.D(adder_1_out), .Q(register_1_q), .clk(clock_1_out), .clr(d_ff_1_q));  // open: en
  not not_1 (not_1_out, comparator_1_gt);
  Comparator #(.width(4)) comparator_1 (.a(register_1_q), .b(in_2), .gt(comparator_1_gt));  // open: eq, lt
  D_Flip_Flop d_ff_1 (.clk(clock_1_out), .D(not_1_out), .Q(d_ff_1_q));  // open: Qn, preset, en, reset
  Register #(.width(1)) register_2 (.D(In), .Q(Out), .clk(not_1_out));  // open: en, clr
endmodule

module loop (
  input  in_1,
  input  in_2
);

  wire and_1_out, muller_1_z, muller_2_z, muller_inv_1_z;

  muller_inv muller_inv_1 (.A(muller_2_z), .B(muller_1_z), .Reset(in_1), .Z(muller_inv_1_z));
  and and_1 (and_1_out, muller_inv_1_z, in_2);
  muller muller_1 (.A(and_1_out), .B(muller_2_z), .Z(muller_1_z), .Reset(in_1));
  muller muller_2 (.A(muller_1_z), .B(and_1_out), .Z(muller_2_z), .Reset(in_1));
endmodule

module muller_inv (
  input  A,
  input  B,
  input  Reset,
  output Z
);

  wire and_1_out, and_2_out, not_1_out, or_1_out, or_2_out;

  not not_1 (not_1_out, B);
  and and_1 (and_1_out, A, not_1_out);
  or or_1 (or_1_out, A, not_1_out);
  or or_2 (or_2_out, and_1_out, and_2_out);
  and and_2 (and_2_out, or_2_out, or_1_out);
  Multiplexer multiplexer_1 (.in0(or_2_out), .in1(1'b1), .out(Z), .sel(Reset));  // open: en
endmodule

module sum (
  input  L_req,
  input  R_ack,
  input  Rst,
  output [3:0] out_4,
  output R_Req,
  output L_ack
);

  wire delay_1_out;
  wire [3:0] adder_1_out, register_1_q;

  Register #(.width(4)) register_1 (.D(4'b0001), .Q(register_1_q), .clk(L_ack));  // open: en, clr
  muller muller_1 (.A(L_req), .B(R_Req), .Z(L_ack), .Reset(Rst));
  Adder #(.width(4)) adder_1 (.a(out_4), .b(register_1_q), .out(adder_1_out));  // open: cin, cout
  Delay delay_1 (.In(L_ack), .in_2(4'b1000), .Out(delay_1_out));
  Register #(.width(4)) register_2 (.D(adder_1_out), .Q(out_4), .clk(R_Req));  // open: en, clr
  muller muller_2 (.A(delay_1_out), .B(R_ack), .Z(R_Req), .Reset(Rst));
endmodule
